# Fritzing sketch NAFSTRCircuit (saved by Fritzing 0.9.0b)
circuit board: 11.1978cm x 5.67858cm
breadboards: 3

parts:
  Part1 = Arduino Uno (Rev3) - ICSP
  Power_plug1 = Power plug
  J1 = female pin header, 2 pins [form="♀ (female)"]
  J2 = male pin header, 2 pins [form="♂ (male)"]
  J3 = female pin header, 2 pins [form="♀ (female)"]
  J4 = male pin header, 2 pins [form="♂ (male)"]
  J5 = female pin header, 2 pins [form="♀ (female)"]
  J6 = male pin header, 2 pins [form="♂ (male)"]
  J7 = female pin header, 2 pins [form="♀ (female)"]
  J8 = male pin header, 2 pins [form="♂ (male)"]
  J13 = Basic Servo
  J14 = Basic Servo
  J15 = Basic Servo
  J16 = Basic Servo
  IC1 = IC, DIP package, 24 pins [chip_label=IC]
  S1 = Round Pushbutton
  R1 = Resistor [tolerance=±5% resistance=10k package=THT]
  S2 = Round Pushbutton
  R2 = Resistor [tolerance=±5% resistance=10k package=THT]
  S3 = Round Pushbutton
  R3 = Resistor [tolerance=±5% resistance=10k package=THT]
  S4 = Round Pushbutton
  R4 = Resistor [tolerance=±5% resistance=10k package=THT]
  S5 = Round Pushbutton
  R5 = Resistor [tolerance=±5% resistance=10k package=THT]
  R6 = Photocell (LDR) [package=THT]
  R7 = Resistor [tolerance=±5% resistance=1k package=THT]
  R8 = Photocell (LDR) [package=THT]
  R9 = Resistor [tolerance=±5% resistance=1k package=THT]
  R10 = Photocell (LDR) [package=THT]
  R11 = Resistor [tolerance=±5% resistance=1k package=THT]
  R12 = Photocell (LDR) [package=THT]
  R13 = Resistor [tolerance=±5% resistance=1k package=THT]
  R18 = Resistor [tolerance=±5% resistance=1k package=THT]
  R19 = Resistor [tolerance=±5% resistance=1k package=THT]
  R20 = Resistor [tolerance=±5% resistance=1k package=THT]
  R21 = Resistor [tolerance=±5% resistance=1k package=THT]
  J17 = Basic Force Sensing Resistor (FSR) [package=THT]
  J18 = Basic Force Sensing Resistor (FSR) [package=THT]
  J19 = Basic Force Sensing Resistor (FSR) [package=THT]
  J20 = Basic Force Sensing Resistor (FSR) [package=THT]
  S6 = SPST Switch [package=switch-spdt]

nets:
  N1: Part1.A0, IC1.pin1
  N2: Part1.A1, IC1.pin10
  N3: Part1.A2, IC1.pin11
  N4: Part1.A3, IC1.pin14
  N5: Part1.A4/SDA, IC1.pin13
  N6: Part1.5V, IC1.pin24, S1.leg1, S2.leg1, S3.leg1, S4.leg1, S5.leg1, R6.pin_0, R8.pin_0, R10.pin_0, R12.pin_0
  N7: Part1.D9_PWM, J16.pulse
  N8: Part1.D3_PWM, J13.pulse
  N9: Part1.D5_PWM, J14.pulse
  N10: Part1.D6_PWM, J15.pulse
  N11: Part1.GND, IC1.pin12, R1.Pin_1, R2.Pin_1, R3.Pin_1, R4.Pin_1, R5.Pin_1, R7.Pin_0, R9.Pin_0, R11.Pin_0, R13.Pin_0
  N12: Power_plug1.VCC, J1.pin1, J3.pin1, J5.pin1, J7.pin1
  N13: Power_plug1.GND, S6.S
  N14: J1.pin2, J3.pin2, J5.pin2, J7.pin2, S6.P
  N15: J2.pin1, J13.vcc
  N16: J2.pin2, J13.gnd
  N17: J4.pin1, J14.vcc
  N18: J4.pin2, J14.gnd
  N19: J6.pin1, J15.vcc
  N20: J6.pin2, J15.gnd
  N21: J8.pin1, J16.vcc
  N22: J8.pin2, J16.gnd
  N23: IC1.pin2, R10.pin_1, R11.Pin_1
  N24: IC1.pin3, R8.pin_1, R9.Pin_1
  N25: IC1.pin4, R6.pin_1, R7.Pin_1
  N26: IC1.pin5, S5.leg0, R5.Pin_0
  N27: IC1.pin6, S4.leg0, R4.Pin_0
  N28: IC1.pin7, S2.leg0, R2.Pin_0
  N29: IC1.pin8, S1.leg0, R1.Pin_0
  N30: IC1.pin9, S3.leg0, R3.Pin_0
  N31: IC1.pin19, R18.Pin_1, J20.pin_1
  N32: IC1.pin20, R19.Pin_1, J19.pin_1
  N33: IC1.pin21, R20.Pin_1, J18.pin_1
  N34: IC1.pin22, R21.Pin_1, J17.pin_1
  N35: IC1.pin23, R12.pin_1, R13.Pin_1
  N36: R18.Pin_0, R19.Pin_0, R20.Pin_0, R21.Pin_0
  N37: J17.pin_0, J18.pin_0, J19.pin_0, J20.pin_0
