# Fritzing sketch NARFSTRCircuit (saved by Fritzing 0.9.2b)
perfboards: 1

parts:
  Limit_Switch = Pushbutton [package=THT]
  Part1 = Arduino Uno (Rev3)
  RGB_Indicator_LED = RGB LED (com. cathode, rgb) [package="5 mm [THT]"]
  R1 = Resistor [tolerance=±5% resistance=10k package=THT]
  Power_plug_-_12V = Power plug
  Linear_Actuator = DC Motor
  Trigger_Switch = Round Pushbutton
  R2 = Resistor [tolerance=±5% resistance=10k package=THT]
  Power_Switch = Toggle Switch [package=THT]
  R3 = Resistor [tolerance=±5% resistance=470 package=THT]
  R4 = Resistor [tolerance=±5% resistance=470 package=THT]
  R5 = Resistor [tolerance=±5% resistance=470 package=THT]
  U1 = mystery part, 15 pins [chip_label="Pololu VNH5019"]
  Retry_DHCP_Switch = Square Pushbutton
  R6 = Resistor [tolerance=±5% resistance=10k package=THT]
  IC1 = IC, DIP package, 4 pins [chip_label="5V UBEC"]

nets:
  N1: Limit_Switch.leg0, Part1.5V, Trigger_Switch.leg0, U1.pin2, U1.pin6, U1.pin8, Retry_DHCP_Switch.leg0, IC1.pin4
  N2: Limit_Switch.leg1, Part1.A0, R1.Pin_0
  N3: Part1.A1, Trigger_Switch.leg1, R2.Pin_0
  N4: Part1.A2, Retry_DHCP_Switch.leg1, R6.Pin_0
  N5: Part1.D8, U1.pin7
  N6: Part1.D9_PWM, U1.pin3
  N7: Part1.D3_PWM, R3.Pin_1
  N8: Part1.D5_PWM, R4.Pin_1
  N9: Part1.D6_PWM, R5.Pin_1
  N10: Part1.D7, U1.pin1
  N11: Part1.GND, RGB_Indicator_LED.common_cathode, R1.Pin_1, R2.Pin_1, Power_Switch.L2, U1.pin9, U1.pin14, R6.Pin_1, IC1.pin2, IC1.pin3
  N12: RGB_Indicator_LED.red_anode, R3.Pin_0
  N13: RGB_Indicator_LED.green_anode, R5.Pin_0
  N14: RGB_Indicator_LED.blue_anode, R4.Pin_0
  N15: Power_plug_-_12V.VCC, U1.pin15, IC1.pin1
  N16: Power_plug_-_12V.GND, Power_Switch.COM
  N17: Linear_Actuator.pin_1, U1.pin13
  N18: Linear_Actuator.pin_2, U1.pin12
